// Logisim project Parte1.circ as structural Verilog: 1 circuit, main circuit main
module main (
  input  [13:0] DIRECCION_DE_MEMORIA,
  input  [23:0] ENTRADA,
  input  R_W_prime,
  input  [13:0] DIRECCION_DE_MEMORIA_2,
  input  [23:0] ENTRADA_2,
  input  R_W_prime_2,
  output [23:0] SALIDA,
  output [23:0] SALIDA_2
);

  wire not_1_out, not_2_out, PULSO_DE_RELOJ_2_out, PULSO_DE_RELOJ_out;
  wire [7:0] ram_2_data, ram_3_data, ram_4_data;
  wire [23:0] ram_1_data;

  Clock PULSO_DE_RELOJ (.out(PULSO_DE_RELOJ_out));
  Clock PULSO_DE_RELOJ_2 (.out(PULSO_DE_RELOJ_2_out));
  RAM #(.addrWidth(14), .dataWidth(24), .bus("asynch")) ram_1 (
    .addr(DIRECCION_DE_MEMORIA), .data(ram_1_data), .sel(PULSO_DE_RELOJ_out), .ld(R_W_prime));  // open: clr
  assign ram_1_data = not_1_out ? ENTRADA : 24'bz;  // Controlled_Buffer controlled_buffer_1
  not not_1 (not_1_out, R_W_prime);
  RAM #(.addrWidth(14), .bus("asynch")) ram_2 (
    .addr(DIRECCION_DE_MEMORIA_2), .data(ram_2_data), .sel(PULSO_DE_RELOJ_2_out), .ld(R_W_prime_2));  // open: clr
  RAM #(.addrWidth(14), .bus("asynch")) ram_3 (
    .addr(DIRECCION_DE_MEMORIA_2), .data(ram_3_data), .sel(PULSO_DE_RELOJ_2_out), .ld(R_W_prime_2));  // open: clr
  RAM #(.addrWidth(14), .bus("asynch")) ram_4 (
    .addr(DIRECCION_DE_MEMORIA_2), .data(ram_4_data), .sel(PULSO_DE_RELOJ_2_out), .ld(R_W_prime_2));  // open: clr
  assign SALIDA = R_W_prime ? ram_1_data : 24'bz;  // Controlled_Buffer controlled_buffer_2
  assign ram_2_data = not_2_out ? ENTRADA_2[7:0] : 8'bz;  // Controlled_Buffer controlled_buffer_3
  assign SALIDA_2 = R_W_prime_2 ? {ram_4_data, ram_3_data, ram_2_data} : 24'bz;  // Controlled_Buffer controlled_buffer_4
  assign ram_3_data = not_2_out ? ENTRADA_2[15:8] : 8'bz;  // Controlled_Buffer controlled_buffer_5
  assign ram_4_data = not_2_out ? ENTRADA_2[23:16] : 8'bz;  // Controlled_Buffer controlled_buffer_6
  not not_2 (not_2_out, R_W_prime_2);

  // Notes on the sheet:
  //   obtener una memoria de 16,384 x 24 bits
  //   Considerar memorias de 16,384 x 8 bits, se quiere
  //   BUS DIRECCIONES
  //   BUS DIRECCIONES
  //   RAM PARTE 1 de 16,384 x 24 bits
  //   BUS DE CONTROL
  //   RAM PARTE 2 de 16,384 x 24 bits
  //   BUS DE CONTROL
  //   BUS DE DATOS
  //   PARTE DE LA MEMORIA MAS SIGNIFICATIVA
  //   BUS DE DATOS
  //   PARTE DE LA MEMORIA MENOS SIGNIFICATIVA
endmodule
