// Logisim project Decodificador.circ as structural Verilog: 2 circuits, main circuit Decodificador
module Decodificador (
  input  [15:0] EC4Dh_EC4Eh,
  output out_2,
  output out_3
);

  wire _4_2_out, _4_out, C_2_out, C_out, D_2_out, D_3_out, D_out, E_out;

  and D (D_out, EC4Dh_EC4Eh[0], ~EC4Dh_EC4Eh[1], EC4Dh_EC4Eh[2], EC4Dh_EC4Eh[3]);  // AND_Gate
  and _4 (_4_out, ~EC4Dh_EC4Eh[4], ~EC4Dh_EC4Eh[5], EC4Dh_EC4Eh[6], ~EC4Dh_EC4Eh[7]);  // AND_Gate
  and C (C_out, ~EC4Dh_EC4Eh[8], ~EC4Dh_EC4Eh[9], EC4Dh_EC4Eh[10], EC4Dh_EC4Eh[11]);  // AND_Gate
  and D_2 (D_2_out, EC4Dh_EC4Eh[12], ~EC4Dh_EC4Eh[13], EC4Dh_EC4Eh[14], EC4Dh_EC4Eh[15]);  // AND_Gate
  and D_3 (D_3_out, EC4Dh_EC4Eh[0], ~EC4Dh_EC4Eh[1], EC4Dh_EC4Eh[2], EC4Dh_EC4Eh[3]);  // AND_Gate
  and _4_2 (_4_2_out, ~EC4Dh_EC4Eh[4], ~EC4Dh_EC4Eh[5], EC4Dh_EC4Eh[6], ~EC4Dh_EC4Eh[7]);  // AND_Gate
  and C_2 (C_2_out, ~EC4Dh_EC4Eh[8], ~EC4Dh_EC4Eh[9], EC4Dh_EC4Eh[10], EC4Dh_EC4Eh[11]);  // AND_Gate
  and E (E_out, ~EC4Dh_EC4Eh[12], EC4Dh_EC4Eh[13], EC4Dh_EC4Eh[14], EC4Dh_EC4Eh[15]);  // AND_Gate
  and Salida (out_2, D_out, _4_out, C_out, D_2_out);
  and Salida_2 (out_3, D_3_out, _4_2_out, C_2_out, E_out);

  // Notes on the sheet:
  //   Decodificador de direcciones
endmodule

module Puerto_de_E_S (
  input  in_1,
  input  [15:0] in_2,
  input  [23:0] DATO_EXTERIOR,
  output [23:0] DATO_DEL_CPU
);

  wire and_1_out, and_2_out, decodificador_1_out_2, decodificador_1_out_3;
  wire [3:0] LATCH_OUT_q, LATCH_OUT_q_2, LATCH_OUT_q_3, LATCH_OUT_q_4, LATCH_OUT_q_5, LATCH_OUT_q_6;

  Decodificador decodificador_1 (.EC4Dh_EC4Eh(in_2), .out_2(decodificador_1_out_2), .out_3(decodificador_1_out_3));
  and and_1 (and_1_out, ~in_1, decodificador_1_out_2);  // AND_Gate
  and and_2 (and_2_out, ~in_1, decodificador_1_out_3);  // AND_Gate
  Register #(.width(24)) LATCH_OUT (
    .D(DATO_DEL_CPU),
    .Q({LATCH_OUT_q_6[0], LATCH_OUT_q_6[1], LATCH_OUT_q_6[2], LATCH_OUT_q_6[3], LATCH_OUT_q_5[0], LATCH_OUT_q_5[1], LATCH_OUT_q_5[2], LATCH_OUT_q_5[3], LATCH_OUT_q_4[0], LATCH_OUT_q_4[1], LATCH_OUT_q_4[2], LATCH_OUT_q_4[3], LATCH_OUT_q_3[0], LATCH_OUT_q_3[1], LATCH_OUT_q_3[2], LATCH_OUT_q_3[3], LATCH_OUT_q_2[0], LATCH_OUT_q_2[1], LATCH_OUT_q_2[2], LATCH_OUT_q_2[3], LATCH_OUT_q[0], LATCH_OUT_q[1], LATCH_OUT_q[2], LATCH_OUT_q[3]}),
    .clk(and_1_out));  // open: en, clr
  Register #(.width(24)) LATCH_IN (.D(DATO_EXTERIOR), .Q(DATO_DEL_CPU), .clk(and_2_out));  // open: en, clr
  Hex_Digit_Display hex_digit_display_1 (.value(LATCH_OUT_q));  // open: dp
  Hex_Digit_Display hex_digit_display_2 (.value(LATCH_OUT_q_2));  // open: dp
  Hex_Digit_Display hex_digit_display_3 (.value(LATCH_OUT_q_4));  // open: dp
  Hex_Digit_Display hex_digit_display_4 (.value(LATCH_OUT_q_3));  // open: dp
  Hex_Digit_Display hex_digit_display_5 (.value(LATCH_OUT_q_5));  // open: dp
  Hex_Digit_Display hex_digit_display_6 (.value(LATCH_OUT_q_6));  // open: dp

  // Notes on the sheet:
  //   DIRECCIONES
  //   Escritura: EC4D
  //   Lectura: EC4E
  //   BUS DIRECCIONES 16 bits
  //   BUS DATOS 24 bits
  //   BUS DE CONTROL
  //   BUS DE CONTROL
  //   PUERTO DE SALIDA Y ENTRADA
  //   BUS DATOS 24 bits
  //   BUS DATOS 24 bits
  //   BUS DATOS 24 bits
endmodule
