// Logisim project Seccion_4_bits.circ as structural Verilog: 2 circuits, main circuit Seccion de entrada y salida de 4 bits
// SALIDA
module Seccion_de_entrada_y_salida_de_4_bits (
  input  [9:0] in_1,
  input  [3:0] PUERTO_DE_ENTRADA
);

  wire _00_out, _01_out, _10_out, _11_out, and_1_out, and_2_out, and_3_out, and_4_out, and_5_out, and_6_out,
       and_7_out, and_8_out, clock_1_out, Decodificador_out_2, Decodificador_out_3,
       Decodificador_rd_wr_prime, not_1_out, not_2_out, not_3_out, not_4_out, not_5_out, not_6_out,
       not_7_out, not_8_out;
  wire [3:0] controlled_buffer_1_out, controlled_buffer_2_out, controlled_buffer_3_out,
       controlled_buffer_4_out, controlled_buffer_5_out, R0_q, R1_q, R2_q, R3_q;

  Clock clock_1 (.out(clock_1_out));
  Decodificador Decodificador (
    .in_1(in_1), .out_2(Decodificador_out_2), .out_3(Decodificador_out_3),
    .RD_WR_prime(Decodificador_rd_wr_prime));
  not not_1 (not_1_out, Decodificador_out_2);
  not not_2 (not_2_out, Decodificador_out_3);
  not not_3 (not_3_out, Decodificador_out_3);
  not not_4 (not_4_out, Decodificador_out_2);
  and _00 (_00_out, not_1_out, not_2_out);
  and and_1 (and_1_out, Decodificador_rd_wr_prime, _00_out);
  and _01 (_01_out, Decodificador_out_2, not_3_out);
  and and_2 (and_2_out, Decodificador_rd_wr_prime, _01_out);
  and _10 (_10_out, not_4_out, Decodificador_out_3);
  and and_3 (and_3_out, Decodificador_rd_wr_prime, _10_out);
  and _11 (_11_out, Decodificador_out_2, Decodificador_out_3);
  and and_4 (and_4_out, Decodificador_rd_wr_prime, _11_out);
  not not_5 (not_5_out, Decodificador_rd_wr_prime);
  and and_5 (and_5_out, not_5_out, _00_out);
  not not_6 (not_6_out, Decodificador_rd_wr_prime);
  and and_6 (and_6_out, not_6_out, _01_out);
  not not_7 (not_7_out, Decodificador_rd_wr_prime);
  and and_7 (and_7_out, not_7_out, _10_out);
  not not_8 (not_8_out, Decodificador_rd_wr_prime);
  and and_8 (and_8_out, not_8_out, _11_out);
  Register #(.width(4)) R0 (.D(controlled_buffer_1_out), .Q(R0_q), .clk(clock_1_out));  // open: en, clr
  assign controlled_buffer_1_out = and_1_out ? PUERTO_DE_ENTRADA : 4'bz;  // Controlled_Buffer controlled_buffer_1
  Register #(.width(4)) R1 (.D(controlled_buffer_2_out), .Q(R1_q), .clk(clock_1_out));  // open: en, clr
  assign controlled_buffer_2_out = and_2_out ? PUERTO_DE_ENTRADA : 4'bz;  // Controlled_Buffer controlled_buffer_2
  assign controlled_buffer_3_out = and_3_out ? PUERTO_DE_ENTRADA : 4'bz;  // Controlled_Buffer controlled_buffer_3
  Register #(.width(4)) R2 (.D(controlled_buffer_3_out), .Q(R2_q), .clk(clock_1_out));  // open: en, clr
  assign controlled_buffer_4_out = and_4_out ? PUERTO_DE_ENTRADA : 4'bz;  // Controlled_Buffer controlled_buffer_4
  Register #(.width(4)) R3 (.D(controlled_buffer_4_out), .Q(R3_q), .clk(clock_1_out));  // open: en, clr
  assign controlled_buffer_5_out = and_5_out ? R0_q : 4'bz;  // Controlled_Buffer controlled_buffer_5
  assign controlled_buffer_5_out = and_6_out ? R1_q : 4'bz;  // Controlled_Buffer controlled_buffer_6
  assign controlled_buffer_5_out = and_7_out ? R2_q : 4'bz;  // Controlled_Buffer controlled_buffer_7
  assign controlled_buffer_5_out = and_8_out ? R3_q : 4'bz;  // Controlled_Buffer controlled_buffer_8
  Hex_Digit_Display hex_digit_display_1 (.value(controlled_buffer_5_out));  // open: dp

  // Notes on the sheet:
  //   L = 0
  //   L = 1
  //   H = 1
  //   Control
  //   Bit 3 siempre en 1
  //   9 8 7 6 5 4 3 2 1 0
  //   1 1 0 0 0 0 x 1 x x
  //   Escritura puerto de salida Bit 4
  //   Lectura puerto de entrada Bit 4
  //   Senal de control
  //   Direcciones de registros
  //   Bus de control
  //   Seccion de entrada y salida de 4 bits
  //   BUS DE DATOS
  //   BUS DE DATOS
  //   BUS DE DATOS
  //   BUS DE DATOS
  //   BUS DE DATOS
  //   DISPLAY SALIDA
endmodule

module Decodificador (
  input  [9:0] in_1,
  output out_2,
  output out_3,
  output RD_WR_prime
);

  wire and_1_out;

  and and_1 (and_1_out, in_1[2], ~in_1[4], ~in_1[5], ~in_1[6], ~in_1[7], in_1[8], in_1[9]);  // AND_Gate
  and and_2 (RD_WR_prime, in_1[3], and_1_out);

  assign out_2 = in_1[0];
  assign out_3 = in_1[1];

  // Notes on the sheet:
  //   9 8 7 6 5 4 3 2 1 0
  //   1 1 0 0 0 0 x 1 x x
  //   Direcciones de registros
  //   DECODIFICADOR DE PUERTO E/S
endmodule
