// Logisim project ALU.circ as structural Verilog: 5 circuits, main circuit ALU
module ALU (
  input  [9:0] in_1,
  input  in_2,
  input  in_3,
  input  in_4,
  input  RS_prime_RD,
  input  C_in,
  output [7:0] Resultado,
  output Bandera_de_zero,
  output Over_Flow,
  output Carry_out
);

  wire adder_1_cout, adder_2_cout, decodificador_1__1, decodificador_1__2, decodificador_1__3,
       decodificador_1__4, decodificador_1__5, decodificador_1__6, decodificador_1__7, decodificador_1__8,
       decodificador_1__9, decodificador_1_a, decodificador_1_b, decodificador_1_c, decodificador_1_d,
       decodificador_1_e, not_1_out, subtractor_1_bout, subtractor_2_bout;
  wire [7:0] A_B_2_out, A_B_3_out, A_B_out, A_out, adder_1_out, adder_2_out, adder_3_out,
       banco_registros_1_out_9, controlled_buffer_1_out, controlled_buffer_2_out, controlled_buffer_3_out,
       controlled_buffer_4_out, controlled_buffer_5_out, controlled_buffer_6_out, controlled_buffer_7_out,
       controlled_buffer_8_out, controlled_buffer_9_out, controlled_buffer_10_out, controlled_buffer_11_out,
       controlled_buffer_12_out, controlled_buffer_13_out, controlled_buffer_14_out, RD_q, RS_q,
       shifter_1_out, shifter_2_out, shifter_3_out, shifter_4_out, subtractor_1_out, subtractor_2_out,
       subtractor_3_out;

  Banco_registros banco_registros_1 (
    .in_4(in_4), .out_9(banco_registros_1_out_9), .entrada_datos(Resultado), .in_5(in_1[0]), .in_6(in_1[1]),
    .in_2(in_1[2]), .in_3(in_1[3]), .Control(in_3), .in_8(in_2));
  Register RS (.D(banco_registros_1_out_9), .Q(RS_q), .clk(not_1_out));  // open: en, clr
  Register RD (.D(banco_registros_1_out_9), .Q(RD_q), .clk(RS_prime_RD));  // open: en, clr
  DECODIFICADOR decodificador_1 (
    .in_1({in_1[9:8], in_1[5:4]}), ._1(decodificador_1__1), ._2(decodificador_1__2), ._3(decodificador_1__3),
    ._4(decodificador_1__4), ._5(decodificador_1__5), ._6(decodificador_1__6), ._7(decodificador_1__7),
    ._8(decodificador_1__8), ._9(decodificador_1__9), .A(decodificador_1_a), .B(decodificador_1_b),
    .C(decodificador_1_c), .D(decodificador_1_d), .E(decodificador_1_e));
  not not_1 (not_1_out, RS_prime_RD);
  Adder adder_1 (.a(RS_q), .b(RD_q), .out(adder_1_out), .cout(adder_1_cout));  // open: cin
  Adder adder_2 (.a(RS_q), .b(RD_q), .out(adder_2_out), .cin(C_in), .cout(adder_2_cout));
  Subtractor subtractor_1 (.a(RD_q), .b(RS_q), .out(subtractor_1_out), .bout(subtractor_1_bout));  // open: bin
  Subtractor subtractor_2 (.a(RD_q), .b(RS_q), .out(subtractor_2_out), .bin(C_in), .bout(subtractor_2_bout));
  Adder adder_3 (.a(RS_q), .b(8'h1), .out(adder_3_out));  // open: cin, cout
  Subtractor subtractor_3 (.a(RS_q), .b(8'h1), .out(subtractor_3_out));  // open: bin, bout
  Shifter shifter_1 (.in(RS_q), .\dist (3'b001), .out(shifter_1_out));
  Shifter #(.shift("lr")) shifter_2 (.in(RS_q), .\dist (3'b001), .out(shifter_2_out));
  Shifter #(.shift("rl")) shifter_3 (.in(RS_q), .\dist (3'b001), .out(shifter_3_out));
  Shifter #(.shift("rr")) shifter_4 (.in(RS_q), .\dist (3'b001), .out(shifter_4_out));
  assign A_B_out = RS_q & RD_q;  // AND_Gate A_B, 8 bits wide
  assign A_B_2_out = RS_q | RD_q;  // OR_Gate A_B_2, 8 bits wide
  assign A_B_3_out = RS_q ^ RD_q;  // XOR_Gate A_B_3, 8 bits wide
  assign A_out = ~RS_q;  // NOT_Gate A, 8 bits wide
  assign controlled_buffer_1_out = decodificador_1__5 ? adder_1_out : 8'bz;  // Controlled_Buffer controlled_buffer_1
  assign controlled_buffer_2_out = decodificador_1__6 ? adder_2_out : 8'bz;  // Controlled_Buffer controlled_buffer_2
  assign controlled_buffer_3_out = decodificador_1__7 ? subtractor_1_out : 8'bz;  // Controlled_Buffer controlled_buffer_3
  assign controlled_buffer_4_out = decodificador_1__8 ? subtractor_2_out : 8'bz;  // Controlled_Buffer controlled_buffer_4
  assign controlled_buffer_5_out = decodificador_1__9 ? adder_3_out : 8'bz;  // Controlled_Buffer controlled_buffer_5
  assign controlled_buffer_6_out = decodificador_1_a ? subtractor_3_out : 8'bz;  // Controlled_Buffer controlled_buffer_6
  assign controlled_buffer_7_out = decodificador_1__1 ? A_B_out : 8'bz;  // Controlled_Buffer controlled_buffer_7
  assign controlled_buffer_8_out = decodificador_1_b ? shifter_1_out : 8'bz;  // Controlled_Buffer controlled_buffer_8
  assign controlled_buffer_9_out = decodificador_1_c ? shifter_2_out : 8'bz;  // Controlled_Buffer controlled_buffer_9
  assign controlled_buffer_10_out = decodificador_1_d ? shifter_3_out : 8'bz;  // Controlled_Buffer controlled_buffer_10
  assign controlled_buffer_11_out = decodificador_1__2 ? A_B_2_out : 8'bz;  // Controlled_Buffer controlled_buffer_11
  assign controlled_buffer_12_out = decodificador_1__3 ? A_B_3_out : 8'bz;  // Controlled_Buffer controlled_buffer_12
  assign controlled_buffer_13_out = decodificador_1__4 ? A_out : 8'bz;  // Controlled_Buffer controlled_buffer_13
  assign controlled_buffer_14_out = decodificador_1_e ? shifter_4_out : 8'bz;  // Controlled_Buffer controlled_buffer_14
  or or_1 (Carry_out, adder_1_cout, adder_2_cout, subtractor_1_bout, subtractor_2_bout);
  Multiplexer #(.select(4), .width(8), .enable("false")) multiplexer_1 (
    .in1(controlled_buffer_7_out), .in2(controlled_buffer_11_out), .in3(controlled_buffer_12_out),
    .in4(controlled_buffer_13_out), .in5(controlled_buffer_1_out), .in6(controlled_buffer_2_out),
    .in7(controlled_buffer_3_out), .in8(controlled_buffer_4_out), .in9(controlled_buffer_5_out),
    .in10(controlled_buffer_6_out), .in11(controlled_buffer_8_out), .in12(controlled_buffer_9_out),
    .in13(controlled_buffer_10_out), .in14(controlled_buffer_14_out), .out(Resultado),
    .sel({in_1[9:8], in_1[5:4]}));  // open: in0, in15
  Comparator comparator_1 (.a(Resultado), .b({8{1'b0}}), .eq(Bandera_de_zero));  // open: gt, lt
  Comparator comparator_2 (.a(Resultado), .b({8{1'b1}}), .lt(Over_Flow));  // open: gt, eq

  // Notes on the sheet:
  //   L = 0
  //   L = 1
  //   CLK R
  //   CLK D
  //   Unidad Aritmetica y Logica (ALU)
  //   Escritura puerto de salida
  //   Lectura puerto de entrada
  //   ACTIVA CLK REGISTROS [R0-R3]
  //   1 ACTIVA RD , 0 ACTIVA RS
  //   B
  //   A
  //   A
endmodule

module ALU_2 (
  input  [7:0] A,
  input  [7:0] B,
  input  [3:0] in_3,
  input  C_in,
  output [7:0] Resultado,
  output Bandera_de_zero,
  output Over_Flow,
  output Carry_out
);

  wire adder_1_cout, adder_2_cout, decodificador_1__1, decodificador_1__2, decodificador_1__3,
       decodificador_1__4, decodificador_1__5, decodificador_1__6, decodificador_1__7, decodificador_1__8,
       decodificador_1__9, decodificador_1_a, decodificador_1_b, decodificador_1_c, decodificador_1_d,
       decodificador_1_e, subtractor_1_bout, subtractor_2_bout;
  wire [7:0] A_B_2_out, A_B_3_out, A_B_out, A_out, adder_1_out, adder_2_out, adder_3_out,
       controlled_buffer_1_out, controlled_buffer_2_out, controlled_buffer_3_out, controlled_buffer_4_out,
       controlled_buffer_5_out, controlled_buffer_6_out, controlled_buffer_7_out, controlled_buffer_8_out,
       controlled_buffer_9_out, controlled_buffer_10_out, controlled_buffer_11_out, controlled_buffer_12_out,
       controlled_buffer_13_out, controlled_buffer_14_out, shifter_1_out, shifter_2_out, shifter_3_out,
       shifter_4_out, subtractor_1_out, subtractor_2_out, subtractor_3_out;

  DECODIFICADOR decodificador_1 (
    .in_1(in_3), ._1(decodificador_1__1), ._2(decodificador_1__2), ._3(decodificador_1__3),
    ._4(decodificador_1__4), ._5(decodificador_1__5), ._6(decodificador_1__6), ._7(decodificador_1__7),
    ._8(decodificador_1__8), ._9(decodificador_1__9), .A(decodificador_1_a), .B(decodificador_1_b),
    .C(decodificador_1_c), .D(decodificador_1_d), .E(decodificador_1_e));
  assign A_B_out = A & B;  // AND_Gate A_B, 8 bits wide
  assign A_B_2_out = A | B;  // OR_Gate A_B_2, 8 bits wide
  assign A_B_3_out = A ^ B;  // XOR_Gate A_B_3, 8 bits wide
  assign A_out = ~A;  // NOT_Gate A, 8 bits wide
  assign controlled_buffer_1_out = decodificador_1__5 ? adder_1_out : 8'bz;  // Controlled_Buffer controlled_buffer_1
  Adder adder_1 (.a(A), .b(B), .out(adder_1_out), .cout(adder_1_cout));  // open: cin
  Adder adder_2 (.a(A), .b(B), .out(adder_2_out), .cin(C_in), .cout(adder_2_cout));
  Subtractor subtractor_1 (.a(B), .b(A), .out(subtractor_1_out), .bout(subtractor_1_bout));  // open: bin
  Subtractor subtractor_2 (.a(B), .b(A), .out(subtractor_2_out), .bin(C_in), .bout(subtractor_2_bout));
  Adder adder_3 (.a(A), .b(8'h1), .out(adder_3_out));  // open: cin, cout
  Subtractor subtractor_3 (.a(A), .b(8'h1), .out(subtractor_3_out));  // open: bin, bout
  Shifter shifter_1 (.in(A), .\dist (3'b001), .out(shifter_1_out));
  Shifter #(.shift("lr")) shifter_2 (.in(A), .\dist (3'b001), .out(shifter_2_out));
  Shifter #(.shift("rl")) shifter_3 (.in(A), .\dist (3'b001), .out(shifter_3_out));
  Shifter #(.shift("rr")) shifter_4 (.in(A), .\dist (3'b001), .out(shifter_4_out));
  assign controlled_buffer_2_out = decodificador_1__6 ? adder_2_out : 8'bz;  // Controlled_Buffer controlled_buffer_2
  assign controlled_buffer_3_out = decodificador_1__7 ? subtractor_1_out : 8'bz;  // Controlled_Buffer controlled_buffer_3
  assign controlled_buffer_4_out = decodificador_1__8 ? subtractor_2_out : 8'bz;  // Controlled_Buffer controlled_buffer_4
  assign controlled_buffer_5_out = decodificador_1__9 ? adder_3_out : 8'bz;  // Controlled_Buffer controlled_buffer_5
  assign controlled_buffer_6_out = decodificador_1_a ? subtractor_3_out : 8'bz;  // Controlled_Buffer controlled_buffer_6
  assign controlled_buffer_7_out = decodificador_1_b ? shifter_1_out : 8'bz;  // Controlled_Buffer controlled_buffer_7
  assign controlled_buffer_8_out = decodificador_1_c ? shifter_2_out : 8'bz;  // Controlled_Buffer controlled_buffer_8
  assign controlled_buffer_9_out = decodificador_1__1 ? A_B_out : 8'bz;  // Controlled_Buffer controlled_buffer_9
  assign controlled_buffer_10_out = decodificador_1__2 ? A_B_2_out : 8'bz;  // Controlled_Buffer controlled_buffer_10
  assign controlled_buffer_11_out = decodificador_1__3 ? A_B_3_out : 8'bz;  // Controlled_Buffer controlled_buffer_11
  assign controlled_buffer_12_out = decodificador_1__4 ? A_out : 8'bz;  // Controlled_Buffer controlled_buffer_12
  assign controlled_buffer_13_out = decodificador_1_d ? shifter_3_out : 8'bz;  // Controlled_Buffer controlled_buffer_13
  assign controlled_buffer_14_out = decodificador_1_e ? shifter_4_out : 8'bz;  // Controlled_Buffer controlled_buffer_14
  or or_1 (Carry_out, adder_1_cout, adder_2_cout, subtractor_1_bout, subtractor_2_bout);
  Multiplexer #(.select(4), .width(8), .enable("false")) multiplexer_1 (
    .in1(controlled_buffer_9_out), .in2(controlled_buffer_10_out), .in3(controlled_buffer_11_out),
    .in4(controlled_buffer_12_out), .in5(controlled_buffer_1_out), .in6(controlled_buffer_2_out),
    .in7(controlled_buffer_3_out), .in8(controlled_buffer_4_out), .in9(controlled_buffer_5_out),
    .in10(controlled_buffer_6_out), .in11(controlled_buffer_7_out), .in12(controlled_buffer_8_out),
    .in13(controlled_buffer_13_out), .in14(controlled_buffer_14_out), .out(Resultado), .sel(in_3));  // open: in0, in15
  Comparator comparator_1 (.a(Resultado), .b({8{1'b0}}), .eq(Bandera_de_zero));  // open: gt, lt
  Comparator comparator_2 (.a(Resultado), .b({8{1'b1}}), .lt(Over_Flow));  // open: gt, eq

  // Notes on the sheet:
  //   B
  //   A
  //   A
  //   Unidad Aritmetica y Logica (ALU)
endmodule

module DECODIFICADOR (
  input  [3:0] in_1,
  output _1,
  output _2,
  output _3,
  output _4,
  output _5,
  output _6,
  output _7,
  output _8,
  output _9,
  output A,
  output B,
  output C,
  output D,
  output E
);

  and and_1 (_1, in_1[0], ~in_1[1], ~in_1[2], ~in_1[3]);  // AND_Gate
  and and_2 (_2, ~in_1[0], in_1[1], ~in_1[2], ~in_1[3]);  // AND_Gate
  and and_3 (_3, in_1[0], in_1[1], ~in_1[2], ~in_1[3]);  // AND_Gate
  and and_4 (_4, ~in_1[0], ~in_1[1], in_1[2], ~in_1[3]);  // AND_Gate
  and and_5 (_5, in_1[0], ~in_1[1], in_1[2], ~in_1[3]);  // AND_Gate
  and and_6 (_6, ~in_1[0], in_1[1], in_1[2], ~in_1[3]);  // AND_Gate
  and and_7 (_7, in_1[0], in_1[1], in_1[2], ~in_1[3]);  // AND_Gate
  and and_8 (_8, ~in_1[0], ~in_1[1], ~in_1[2], in_1[3]);  // AND_Gate
  and and_9 (_9, in_1[0], ~in_1[1], ~in_1[2], in_1[3]);  // AND_Gate
  and and_10 (A, ~in_1[0], in_1[1], ~in_1[2], in_1[3]);  // AND_Gate
  and and_11 (B, in_1[0], in_1[1], ~in_1[2], in_1[3]);  // AND_Gate
  and and_12 (C, ~in_1[0], ~in_1[1], in_1[2], in_1[3]);  // AND_Gate
  and and_13 (D, in_1[0], ~in_1[1], in_1[2], in_1[3]);  // AND_Gate
  and and_14 (E, ~in_1[0], in_1[1], in_1[2], in_1[3]);  // AND_Gate

  // Notes on the sheet:
  //   Decodificador OP
endmodule

module Banco_registros (
  input  Control,
  input  in_2,
  input  in_3,
  input  in_4,
  input  in_5,
  input  in_6,
  input  [7:0] entrada_datos,
  input  in_8,
  output [7:0] out_9
);

  wire _00_out, _01_out, _10_out, _11_out, and_1_out, and_2_out, and_3_out, and_4_out, and_5_out, and_6_out,
       and_7_out, and_8_out, controlled_buffer_1_out, controlled_buffer_2_out, not_1_out, not_2_out,
       not_3_out, not_4_out, not_5_out, not_6_out, not_7_out, not_8_out, not_9_out;
  wire [7:0] controlled_buffer_5_out, controlled_buffer_6_out, controlled_buffer_7_out,
       controlled_buffer_8_out, R0_q, R1_q, R2_q, R3_q;

  assign controlled_buffer_1_out = not_1_out ? in_2 : 1'bz;  // Controlled_Buffer controlled_buffer_1
  assign controlled_buffer_2_out = not_1_out ? in_3 : 1'bz;  // Controlled_Buffer controlled_buffer_2
  not not_1 (not_1_out, in_8);
  assign controlled_buffer_1_out = in_8 ? in_5 : 1'bz;  // Controlled_Buffer controlled_buffer_3
  assign controlled_buffer_2_out = in_8 ? in_6 : 1'bz;  // Controlled_Buffer controlled_buffer_4
  not not_2 (not_2_out, controlled_buffer_1_out);
  not not_3 (not_3_out, controlled_buffer_2_out);
  not not_4 (not_4_out, controlled_buffer_2_out);
  not not_5 (not_5_out, controlled_buffer_1_out);
  and _00 (_00_out, not_2_out, not_3_out);
  and and_1 (and_1_out, in_4, _00_out);
  and _01 (_01_out, controlled_buffer_1_out, not_4_out);
  and and_2 (and_2_out, in_4, _01_out);
  and _10 (_10_out, not_5_out, controlled_buffer_2_out);
  and and_3 (and_3_out, in_4, _10_out);
  and _11 (_11_out, controlled_buffer_1_out, controlled_buffer_2_out);
  and and_4 (and_4_out, in_4, _11_out);
  not not_6 (not_6_out, in_4);
  and and_5 (and_5_out, not_6_out, _00_out);
  not not_7 (not_7_out, in_4);
  and and_6 (and_6_out, not_7_out, _01_out);
  not not_8 (not_8_out, in_4);
  and and_7 (and_7_out, not_8_out, _10_out);
  not not_9 (not_9_out, in_4);
  and and_8 (and_8_out, not_9_out, _11_out);
  Register R0 (.D(controlled_buffer_5_out), .Q(R0_q), .clk(Control));  // open: en, clr
  assign controlled_buffer_5_out = and_1_out ? entrada_datos : 8'bz;  // Controlled_Buffer controlled_buffer_5
  assign controlled_buffer_6_out = and_2_out ? entrada_datos : 8'bz;  // Controlled_Buffer controlled_buffer_6
  Register R1 (.D(controlled_buffer_6_out), .Q(R1_q), .clk(Control));  // open: en, clr
  assign controlled_buffer_7_out = and_3_out ? entrada_datos : 8'bz;  // Controlled_Buffer controlled_buffer_7
  Register R2 (.D(controlled_buffer_7_out), .Q(R2_q), .clk(Control));  // open: en, clr
  Register R3 (.D(controlled_buffer_8_out), .Q(R3_q), .clk(Control));  // open: en, clr
  assign controlled_buffer_8_out = and_4_out ? entrada_datos : 8'bz;  // Controlled_Buffer controlled_buffer_8
  assign out_9 = and_5_out ? R0_q : 8'bz;  // Controlled_Buffer controlled_buffer_9
  assign out_9 = and_6_out ? R1_q : 8'bz;  // Controlled_Buffer controlled_buffer_10
  assign out_9 = and_7_out ? R2_q : 8'bz;  // Controlled_Buffer controlled_buffer_11
  assign out_9 = and_8_out ? R3_q : 8'bz;  // Controlled_Buffer controlled_buffer_12

  // Notes on the sheet:
  //   L = 0
  //   L = 1
  //   H = 1
  //   Bit 3 siempre en 1
  //   9 8 7 6 5 4 3 2 1 0
  //   1 1 0 0 0 0 x 1 x x
  //   Escritura puerto de salida Bit 4
  //   Lectura puerto de entrada Bit 4
  //   Senal de control
  //   Direcciones de registros
  //   Bus de control
  //   Seccion de entrada y salida de 4 bits
  //   BUS DE DATOS
  //   BUS DE DATOS
  //   BUS DE DATOS
  //   BUS DE DATOS
  //   BUS DE DATOS
  //   SALIDA DATOS
endmodule

module DECODIFICADOR_CARRY (
  input  in_1,
  input  in_2,
  input  CARRY_IN
);

  wire and_1_out, nand_1_out;

  and and_1 (and_1_out, in_1, in_2);
  nand nand_1 (nand_1_out, and_1_out, CARRY_IN);
endmodule
